// Logisim project Ctl_Load_Store.circ as structural Verilog: 1 circuit, main circuit Load_Store
module Load_Store (
  input  Enable,
  input  [15:0] Instruction,
  input  Clk,
  input  Reset,
  input  [31:0] Stack_Pointer,
  output Store,
  output Load,
  output PC_Hold,
  output [2:0] Rmd,
  output [31:0] RAM_Addr
);

  wire and_1_out, d_ff_1_q, not_1_out;
  wire [2:0] bit_extender_1_out;
  wire [31:0] adder_1_out, bit_extender_2_out, bit_extender_3_out;

  and and_1 (and_1_out, ~d_ff_1_q, Load);  // AND_Gate
  D_Flip_Flop d_ff_1 (.D(and_1_out), .clk(Clk), .Q(d_ff_1_q), .reset(Reset));  // open: Qn, preset
  and and_2 (PC_Hold, d_ff_1_q, Enable);
  assign bit_extender_1_out = {{2{Enable}}, Enable};  // Bit_Extender bit_extender_1
  assign Rmd = bit_extender_1_out & Instruction[10:8];  // AND_Gate and_3, 3 bits wide
  assign bit_extender_2_out = {{24{Instruction[7]}}, Instruction[7:0]};  // Bit_Extender bit_extender_2
  Adder #(.width(32)) adder_1 (.a(bit_extender_2_out), .b(Stack_Pointer), .out(adder_1_out));  // open: cin, cout
  assign bit_extender_3_out = {{31{Enable}}, Enable};  // Bit_Extender bit_extender_3
  and and_4 (Load, Instruction[11], Enable);
  assign RAM_Addr = bit_extender_3_out & adder_1_out;  // AND_Gate and_5, 32 bits wide
  not not_1 (not_1_out, Load);
  and and_6 (Store, not_1_out, Enable);

  // Other names for the same wires on the sheet: Clock = Clk; imm8[7:0] = Instruction[7:0];
  //   Rmd_t[2:0] = Instruction[10:8]; BitOnze = Instruction[11]; Stack_P[31:0] = Stack_Pointer

  // Notes on the sheet:
  //   Instruction: pull=down
  //   Delay load and hold PC for 1 cycle for the RAM to send out requested data 
endmodule
