// Logisim project Ctl_Shift_Add_Sub_Mov.circ as structural Verilog: 1 circuit, main circuit Shift_Add_Sub_Mov
module Shift_Add_Sub_Mov (
  input  [15:0] Instruction,
  input  Enable,
  output [2:0] Rm,
  output Carry,
  output [2:0] Rn,
  output [2:0] Rd,
  output [4:0] Imm5,
  output [31:0] Imm32,
  output Imm32_Enable,
  output [3:0] Flags_Update_Mask,
  output [3:0] ALU_Opcode
);

  wire a, ADD_I, ADD_IMM, ADD_R, ADD_SUB, and_1_out, and_2_out, and_3_out, and_5_out, and_6_out, and_11_out,
       and_12_out, and_13_out, and_16_out, and_17_out, and_18_out, and_20_out, and_22_out, ASR, b, c, CMP, d,
       LSL, LSR, MOVE, not_1_out, not_2_out, not_3_out, not_4_out, not_5_out, not_6_out, not_7_out,
       not_8_out, not_9_out, or_1_out, or_2_out, or_3_out, or_4_out, or_5_out, or_10_out, or_17_out, SUB_I,
       SUB_IMM, SUB_R;
  wire [1:0] or_14_out;
  wire [2:0] imm3, RD1, RD2, RD3, RD4, RDN5, RM1, RM2, RN1, RN2;
  wire [3:0] bit_extender_8_out, bit_extender_10_out, or_6_out;
  wire [7:0] imm8;
  wire [15:0] and_7_out, and_8_out, bit_extender_1_out, bit_extender_2_out, bit_extender_3_out,
       bit_extender_4_out, bit_extender_5_out, bit_extender_6_out, Instr;
  wire [15:9] and_14_out, and_15_out;
  wire [15:11] and_10_out;
  wire [31:0] bit_extender_7_out, bit_extender_9_out, multiplexer_1_out, negator_1_out;

  assign bit_extender_1_out = {{15{Enable}}, Enable};  // Bit_Extender bit_extender_1
  Decoder #(.select(3)) decoder_1 (
    .out0(LSL), .out1(LSR), .out2(ASR), .out3(ADD_SUB), .out4(MOVE), .out5(CMP), .out6(ADD_IMM),
    .out7(SUB_IMM), .sel({a, b, c}));  // open: en
  Decoder #(.select(2)) decoder_2 (
    .out0(ADD_R), .out1(SUB_R), .out2(ADD_I), .out3(SUB_I), .sel({Instr[10], d}));  // open: en
  or or_1 (or_1_out, ADD_R, SUB_R);
  or or_2 (or_2_out, ADD_I, SUB_I);
  or or_3 (or_3_out, LSL, LSR, ASR);
  or or_4 (or_4_out, MOVE, CMP);
  or or_5 (or_5_out, ADD_IMM, SUB_IMM);
  not not_1 (not_1_out, a);
  and and_1 (and_1_out, not_1_out, c, not_2_out);
  not not_2 (not_2_out, b);
  not not_3 (not_3_out, d);
  and and_2 (and_2_out, not_3_out, c, not_4_out);
  not not_4 (not_4_out, a);
  and and_3 (and_3_out, a, not_5_out);
  not not_5 (not_5_out, c);
  not not_6 (not_6_out, b);
  assign {Instr[15:14], a, b, c, Instr[10], d, Instr[8:0]} = Instruction & bit_extender_1_out;  // AND_Gate and_4, 16 bits wide
  and and_5 (and_5_out, or_1_out, ADD_SUB);
  and and_6 (and_6_out, or_2_out, ADD_SUB);
  assign bit_extender_2_out = {{15{or_3_out}}, or_3_out};  // Bit_Extender bit_extender_2
  assign bit_extender_3_out = {{15{or_4_out}}, or_4_out};  // Bit_Extender bit_extender_3
  assign {and_7_out[15:11], RD4, and_7_out[7:0]} = bit_extender_3_out & {Instr[15:14], a, b, c, Instr[10], d, Instr[8:0]};  // AND_Gate and_7, 16 bits wide
  assign bit_extender_4_out = {{15{or_5_out}}, or_5_out};  // Bit_Extender bit_extender_4
  assign {and_8_out[15:11], RDN5, and_8_out[7:0]} = bit_extender_4_out & {Instr[15:14], a, b, c, Instr[10], d, Instr[8:0]};  // AND_Gate and_8, 16 bits wide
  or or_6 (or_6_out[0], and_1_out, and_2_out, and_3_out);
  not not_7 (not_7_out, a);
  not not_8 (not_8_out, b);
  and and_9 (or_6_out[3], a, not_6_out);
  assign bit_extender_5_out = {{15{and_5_out}}, and_5_out};  // Bit_Extender bit_extender_5
  assign bit_extender_6_out = {{15{and_6_out}}, and_6_out};  // Bit_Extender bit_extender_6
  assign {and_10_out, Imm5, RM2, RD3} = bit_extender_2_out & {Instr[15:14], a, b, c, Instr[10], d, Instr[8:0]};  // AND_Gate and_10, 16 bits wide
  and and_11 (and_11_out, not_7_out, not_8_out);
  and and_12 (and_12_out, d, c);
  and and_13 (and_13_out, c, a);
  assign {and_14_out, RM1, RN1, RD1} = bit_extender_5_out & {Instr[15:14], a, b, c, Instr[10], d, Instr[8:0]};  // AND_Gate and_14, 16 bits wide
  assign {and_15_out, imm3, RN2, RD2} = bit_extender_6_out & {Instr[15:14], a, b, c, Instr[10], d, Instr[8:0]};  // AND_Gate and_15, 16 bits wide
  assign imm8 = and_7_out[7:0] | and_8_out[7:0];  // OR_Gate or_7, 8 bits wide
  or or_8 (or_6_out[1], and_11_out, and_12_out, and_13_out);
  assign Rm = RM1 | RM2;  // OR_Gate or_9, 3 bits wide
  assign bit_extender_7_out = {{24{1'b0}}, imm8};  // Bit_Extender bit_extender_7
  or or_10 (or_10_out, ADD_I, SUB_I);
  and and_16 (and_16_out, c, b);
  and and_17 (and_17_out, c, a);
  and and_18 (and_18_out, a, b);
  assign ALU_Opcode = {or_6_out[3], b, or_6_out[1:0]} & bit_extender_8_out;  // AND_Gate and_19, 4 bits wide
  assign bit_extender_8_out = {{3{Enable}}, Enable};  // Bit_Extender bit_extender_8
  assign Rn = RN2 | RN1 | RDN5 | RM2;  // OR_Gate or_11, 3 bits wide
  assign Rd = RD1 | RD2 | RD3 | RD4 | RDN5;  // OR_Gate or_12, 3 bits wide
  Negator #(.width(32)) negator_1 (.in(bit_extender_7_out), .out(negator_1_out));
  and and_20 (and_20_out, or_10_out, ADD_SUB);
  not not_9 (not_9_out, a);
  or or_13 (or_14_out[1], not_9_out, b, c);
  or or_14 (or_14_out[0], and_16_out, and_17_out, and_18_out);
  Multiplexer #(.width(32)) multiplexer_1 (
    .in0(bit_extender_7_out), .in1(negator_1_out), .out(multiplexer_1_out), .sel(MOVE));
  or or_15 (Imm32_Enable, and_20_out, MOVE, CMP, SUB_IMM, ADD_IMM);
  assign bit_extender_9_out = {{29{1'b0}}, imm3};  // Bit_Extender bit_extender_9
  assign bit_extender_10_out = {{3{Enable}}, Enable};  // Bit_Extender bit_extender_10
  assign Imm32 = bit_extender_9_out | multiplexer_1_out;  // OR_Gate or_16, 32 bits wide
  assign Flags_Update_Mask = {2'b11, or_14_out} & bit_extender_10_out;  // AND_Gate and_21, 4 bits wide
  or or_17 (or_17_out, SUB_I, SUB_R);
  and and_22 (and_22_out, or_17_out, ADD_IMM);
  or or_18 (Carry, and_22_out, SUB_IMM);

  // Other names for the same wires on the sheet: Instr (some bits) = {a, b, c, d}

  // Notes on the sheet:
  //   Pull output low on Enable = 0
endmodule
